# Fritzing sketch schemat_cablage (saved by Fritzing 0.9.4)
breadboards: 1

parts:
  Composant1 = Arduino Uno (Rev3)
  Composant4 = Real Time Clock Module - DS1307 RTC Breakout Board
  J1 = Piezo Speaker
  Composant5 = LCD1602-I2C
  Composant6 = LED Matrix - Serial Interface - Red/Green/Blue
  Composant7 = LED Matrix - Serial Interface - Red/Green/Blue
  R1 = 100 Ω Resistor [package=THT]
  S2 = Round Pushbutton
  S3 = Round Pushbutton
  S4 = Round Pushbutton
  S5 = Round Pushbutton
  S6 = SPST Switch [package=switch-spdt-smd]
  C1 = Electrolytic Capacitor [capacitance=1µF package="100 mil [THT, electrolytic]"]
  C2 = Electrolytic Capacitor [capacitance=1µF package="100 mil [THT, electrolytic]"]
  C3 = Electrolytic Capacitor [capacitance=1µF package="100 mil [THT, electrolytic]"]
  C4 = Electrolytic Capacitor [capacitance=1µF package="100 mil [THT, electrolytic]"]
  C5 = Electrolytic Capacitor [capacitance=1µF package="100 mil [THT, electrolytic]"]
  R2 = Resistor [tolerance=±5% resistance=220 package=THT]
  R3 = Resistor [tolerance=±5% resistance=220 package=THT]
  R4 = Resistor [tolerance=±5% resistance=220 package=THT]
  R5 = Resistor [tolerance=±5% resistance=220 package=THT]
  R6 = Resistor [tolerance=±5% resistance=220 package=THT]

nets:
  N1: Composant1.A4/SDA, Composant4.SDA, Composant5.SDA
  N2: Composant1.A5/SCL, Composant4.SCL, Composant5.SCL
  N3: Composant1.D8, Composant7.SCK
  N4: Composant1.D9_PWM, Composant7.CS
  N5: Composant1.D10_PWM/SS, Composant7.MOSI
  N6: Composant1.D11_PWM/MOSI, Composant6.SCK
  N7: Composant1.D12/MISO, Composant6.CS
  N8: Composant1.D13/SCK, Composant6.MOSI
  N9: Composant1.D2, S6.S
  GND: Composant1.D3_PWM, Composant1.D4, Composant1.D5_PWM, Composant1.D6_PWM, Composant6.GND, Composant7.GND, S2.leg1, S3.leg1, S4.leg1, S5.leg1, S6.O, C1.+, C2.+, C3.+, C4.+, C5.+
  N10: Composant1.D7, J1.pin2
  5V: Composant1.5V, Composant4.5V, Composant5.VCC
  GND_2: Composant1.GND, Composant4.GND, Composant5.GND
  N11: J1.pin1, R1.Pin_1
  VCC: Composant6.VCC, Composant7.VCC, R1.100_ohm, S2.leg0, S3.leg0, S4.leg0, S5.leg0, S6.P, C1.-, C2.-, C3.-, C4.-, C5.-, R2.Pin_0, R2.Pin_1, R3.Pin_0, R3.Pin_1, R4.Pin_0, R4.Pin_1, R5.Pin_0, R5.Pin_1, R6.Pin_0, R6.Pin_1

custom parts:
  LCD1602-I2C: A standard character display, usually with 2x16 characters. Comes in many colors with LCM1602 IIC attached.
  100 Ω Resistor: A generic resistor (0.25W)
